# Fritzing sketch sketch (saved by Fritzing 0.9.9b)

parts:
  part = ESP32S-HiLetgo [part_number=ESP32S-HiLetgo]
  part_2 = LCD1602-I2C
  part_3 = smd LED [color="Red (633nm)" package="0805 [SMD]"]
  part_4 = Resistor [tolerance=±5% resistance=130 package="0603 [SMD]"]
  MQ-2 = MQ-2 [package="DIP (Dual Inline) [THT]"]
  MQ-7 = MQ-2 [package="DIP (Dual Inline) [THT]"]
  MQ-9 = MQ-2 [package="DIP (Dual Inline) [THT]"]

nets:
  N1: part.GPIO34, MQ-9.pin4
  N2: part.GPIO32, MQ-7.pin4
  N3: part.GPIO33, MQ-2.pin4
  GND: part.GND, part_2.GND, part_3.anode, MQ-2.pin2, MQ-7.pin2, MQ-9.pin2
  N4: part.GPIO9, part_2.VCC, MQ-2.pin1, MQ-7.pin1, MQ-9.pin1
  N5: part.GPIO19, part_4.Pin_1
  N6: part.GPIO21, part_2.SDA
  N7: part.GPIO22, part_2.SCL
  N8: part_3.cathode, part_4.Pin_0

custom parts:
  ESP32S-HiLetgo: HiLetgo ESP-WROOM-32 ESP32 ESP-32S Development Board 2.4GHz Dual-Mode WiFi + Bluetooth Dual Cores Microcontroller The ESP32 integrated with Antenna switches, RF Balun, power amplifiers, low-noise amplifiers, filters, and management modules, and the entire solution occupies the least area of PCB. 2.4 GHz Wi-Fi plus Bluetooth dual-mode chip, with TSMC Ultra-low power consumption 40nm technology,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
  LCD1602-I2C: A standard character display, usually with 2x16 characters. Comes in many colors with LCM1602 IIC attached.
  MQ-2: MQ-2 Gas Sensor module
